// Digital circuit CC.dig as structural Verilog
module CC (
  input  [6:0] OPCD,
  input  [2:0] F3,
  input  [6:0] F7,
  input  [31:0] SULA,
  output IMM,
  output BRG,
  output STR,
  output LD,
  output [1:0] PC,
  output [1:0] DADO,
  output [1:0] TPIMM,
  output [2:0] ULA
);

  wire _0000011, _0010011, _0100011, _0110011, _1100011, _1100111, _1101111, and_1_out, and_2_out, and_3_out,
       and_4_out, and_5_out, and_6_out, and_7_out, and_8_out, and_10_out, and_11_out, and_12_out, and_14_out,
       and_15_out, and_16_out, and_18_out, and_19_out, and_20_out, and_22_out, and_23_out, and_24_out,
       and_26_out, and_27_out, and_28_out, and_30_out, and_31_out, and_32_out, and_34_out, and_35_out,
       and_36_out, and_37_out, and_38_out, and_39_out, and_40_out, and_41_out, and_42_out, and_43_out,
       and_44_out, and_45_out, and_46_out, and_47_out, and_48_out, and_49_out, and_50_out, and_51_out,
       and_52_out, and_53_out, and_54_out, not_1_out, not_2_out, not_3_out, not_4_out, not_5_out, not_6_out,
       not_7_out, not_8_out, not_9_out, not_10_out, not_11_out, not_12_out, not_13_out, not_14_out,
       not_15_out, not_16_out, not_17_out, not_18_out, not_19_out, not_20_out, not_21_out, not_22_out,
       not_23_out, not_24_out, not_25_out, not_26_out, not_27_out, not_28_out, not_29_out, not_30_out,
       not_31_out, not_32_out, not_33_out, not_34_out, not_35_out, not_36_out, not_37_out, not_38_out,
       not_39_out, not_40_out, not_41_out, not_42_out, not_43_out, not_44_out, not_45_out, not_46_out,
       or_1_out, or_3_out, or_7_out, or_8_out, or_9_out, or_10_out, or_11_out, or_12_out;
  wire [2:0] or_4_out;
  wire [3:3] rom_1_d;

  and and_1 (and_1_out, not_1_out, not_2_out, not_3_out, SULA[0]);
  not not_1 (not_1_out, F3[0]);
  not not_2 (not_2_out, F3[1]);
  and and_2 (and_2_out, F3[0], not_4_out, not_5_out, not_6_out);
  not not_3 (not_3_out, F3[2]);
  or or_1 (or_1_out, and_1_out, and_2_out, and_4_out, and_6_out);
  not not_4 (not_4_out, F3[1]);
  not not_5 (not_5_out, F3[2]);
  not not_6 (not_6_out, SULA[0]);
  or or_2 (PC[1], and_3_out, and_5_out);
  and and_3 (and_3_out, or_1_out, _1100011);
  and and_4 (and_4_out, not_8_out, not_7_out, F3[2], SULA[0]);
  not not_7 (not_7_out, F3[1]);
  not not_8 (not_8_out, F3[0]);
  and and_5 (and_5_out, rom_1_d[3], or_3_out);
  and and_6 (and_6_out, F3[0], not_9_out, F3[2], not_10_out);
  not not_9 (not_9_out, F3[1]);
  or or_3 (or_3_out, _0100011, _0000011, _1100111, _1101111, _0010011, _0110011);
  not not_10 (not_10_out, SULA[0]);
  ROM #(.AddrBits(3), .Bits(10)) rom_1 (
    .A(or_4_out), .sel(1'b1), .D({IMM, TPIMM, BRG, STR, LD, rom_1_d[3], PC[0], DADO}));
  // Probe on or_4_out
  not not_11 (not_11_out, OPCD[6]);
  and and_7 (and_7_out, OPCD[5], not_11_out);
  or or_4 (or_4_out[0], _1100111, _1100011, _0000011, _0110011);
  or or_5 (or_4_out[1], _1100111, _1101111, _0000011, _0010011);
  or or_6 (or_4_out[2], _1100111, _1101111, _1100011, _0100011);
  not not_12 (not_12_out, OPCD[3]);
  not not_13 (not_13_out, OPCD[2]);
  and and_8 (and_8_out, not_12_out, OPCD[4]);
  and and_9 (_0110011, and_10_out, and_8_out, and_7_out);
  not not_14 (not_14_out, OPCD[6]);
  and and_10 (and_10_out, OPCD[0], OPCD[1], not_13_out);
  not not_15 (not_15_out, OPCD[5]);
  and and_11 (and_11_out, not_15_out, not_14_out);
  not not_16 (not_16_out, OPCD[3]);
  not not_17 (not_17_out, OPCD[2]);
  and and_12 (and_12_out, not_16_out, OPCD[4]);
  and and_13 (_0010011, and_14_out, and_12_out, and_11_out);
  and and_14 (and_14_out, OPCD[0], OPCD[1], not_17_out);
  not not_18 (not_18_out, OPCD[6]);
  not not_19 (not_19_out, OPCD[5]);
  and and_15 (and_15_out, not_19_out, not_18_out);
  not not_20 (not_20_out, OPCD[4]);
  not not_21 (not_21_out, OPCD[3]);
  and and_16 (and_16_out, not_21_out, not_20_out);
  and and_17 (_0000011, and_18_out, and_16_out, and_15_out);
  not not_22 (not_22_out, OPCD[2]);
  and and_18 (and_18_out, OPCD[0], OPCD[1], not_22_out);
  not not_23 (not_23_out, OPCD[6]);
  and and_19 (and_19_out, OPCD[5], not_23_out);
  not not_24 (not_24_out, OPCD[4]);
  not not_25 (not_25_out, OPCD[3]);
  and and_20 (and_20_out, not_25_out, not_24_out);
  and and_21 (_0100011, and_22_out, and_20_out, and_19_out);
  not not_26 (not_26_out, OPCD[2]);
  and and_22 (and_22_out, OPCD[0], OPCD[1], not_26_out);
  not not_27 (not_27_out, OPCD[4]);
  and and_23 (and_23_out, OPCD[5], OPCD[6]);
  not not_28 (not_28_out, OPCD[3]);
  not not_29 (not_29_out, OPCD[2]);
  and and_24 (and_24_out, not_28_out, not_27_out);
  and and_25 (_1100011, and_26_out, and_24_out, and_23_out);
  and and_26 (and_26_out, OPCD[0], OPCD[1], not_29_out);
  not not_30 (not_30_out, OPCD[4]);
  and and_27 (and_27_out, OPCD[5], OPCD[6]);
  and and_28 (and_28_out, OPCD[3], not_30_out);
  and and_29 (_1101111, and_30_out, and_28_out, and_27_out);
  and and_30 (and_30_out, OPCD[0], OPCD[1], OPCD[2]);
  and and_31 (and_31_out, OPCD[5], OPCD[6]);
  not not_31 (not_31_out, OPCD[4]);
  not not_32 (not_32_out, OPCD[3]);
  and and_32 (and_32_out, not_32_out, not_31_out);
  and and_33 (_1100111, and_34_out, and_32_out, and_31_out);
  and and_34 (and_34_out, OPCD[0], OPCD[1], OPCD[2]);
  not not_33 (not_33_out, F3[0]);
  not not_34 (not_34_out, F3[1]);
  not not_35 (not_35_out, F3[2]);
  and and_35 (and_35_out, not_35_out, not_34_out, not_33_out);
  not not_36 (not_36_out, F3[1]);
  not not_37 (not_37_out, F3[2]);
  and and_36 (and_36_out, not_37_out, not_36_out, F3[0]);
  not not_38 (not_38_out, F3[0]);
  not not_39 (not_39_out, F3[2]);
  and and_37 (and_37_out, not_39_out, F3[1], not_38_out);
  not not_40 (not_40_out, F3[1]);
  not not_41 (not_41_out, F3[0]);
  and and_38 (and_38_out, F3[2], not_40_out, not_41_out);
  not not_42 (not_42_out, F3[1]);
  and and_39 (and_39_out, F3[2], not_42_out, F3[0]);
  not not_43 (not_43_out, F3[0]);
  and and_40 (and_40_out, F3[2], F3[1], not_43_out);
  and and_41 (and_41_out, F3[2], F3[1], F3[0]);
  not not_44 (not_44_out, F7[0]);
  not not_45 (not_45_out, F7[1]);
  and and_42 (and_42_out, not_45_out, _0110011, not_44_out);
  or or_7 (or_7_out, and_42_out, _0010011);
  or or_8 (or_8_out, and_36_out, and_35_out);
  or or_9 (or_9_out, and_39_out, and_38_out);
  not not_46 (not_46_out, F7[0]);
  and and_43 (and_43_out, F7[1], _0110011, not_46_out);
  and and_44 (and_44_out, or_7_out, and_41_out);
  and and_45 (and_45_out, or_7_out, and_37_out);
  and and_46 (and_46_out, or_8_out, _1100011);
  and and_47 (and_47_out, or_9_out, _1100011);
  or or_10 (or_10_out, _0000011, _0100011);
  and and_48 (and_48_out, or_7_out, and_35_out);
  and and_49 (and_49_out, and_35_out, _1100111);
  and and_50 (and_50_out, and_37_out, or_10_out);
  and and_51 (and_51_out, or_7_out, and_38_out);
  and and_52 (and_52_out, and_43_out, and_35_out);
  and and_53 (and_53_out, or_7_out, and_40_out);
  or or_11 (or_11_out, and_44_out, and_46_out);
  and and_54 (and_54_out, or_7_out, and_36_out);
  or or_12 (or_12_out, and_45_out, and_47_out);
  or or_13 (ULA[0], and_48_out, and_49_out, and_50_out, and_51_out, or_11_out, or_12_out);
  or or_14 (ULA[1], and_51_out, and_52_out, and_54_out, and_53_out, or_12_out);
  or or_15 (ULA[2], or_11_out, and_54_out, or_12_out);

  // Notes on the sheet:
  //   contents of rom_1 (hex, n*v repeats v):
  //   0,47,3c7,3d6,324,8c,4d,3c9
endmodule
