// Digital circuit ProjetoMicroarquitetural.dig as structural Verilog
module ProjetoMicroarquitetural (
  input  clk
);

  wire IMM, LD, MWRITE, STR, ZERO;
  wire [1:0] DADO, PC, TPIMM;
  wire [2:0] F3, ULA;
  wire [4:0] RD, RS1, RS2;
  wire [6:0] F7, OPCODE;
  wire [31:0] add_1_s, add_2_s, add_3_s, brg_1_s1, MDD_d, multiplexer_1_out, multiplexer_2_out, SDADO, SIMM,
       SPC, SRS2, SULA;

  REG u_PC (.CLK(clk), .E(multiplexer_1_out), .S(SPC));
  Multiplexer #(.Selector_Bits(2), .Bits(32)) multiplexer_1 (
    .sel(PC), .in_0(SPC), .in_1(add_2_s), .in_2(SULA), .in_3(add_1_s), .out(multiplexer_1_out));
  ROM #(.AddrBits(7), .isProgramMemory("true"), .Bits(32)) MI (
    .A(SPC[6:0]), .sel(1'b1), .D({F7, RS2, RS1, F3, RD, OPCODE}));
  ADD add_1 (.RS1(SPC), .RS2(SIMM), .S(add_1_s));  // open: Cout
  ADD add_2 (.RS1(SPC), .RS2(32'h4), .S(add_2_s));  // open: Cout
  CC cc_1 (
    .OPCD(OPCODE), .DADO(DADO), .PC(PC), .LD(LD), .STR(STR), .BRG(MWRITE), .TPIMM(TPIMM), .IMM(IMM), .F3(F3),
    .ZERO(ZERO), .F7(F7), .ULA(ULA), .SULA(SULA));
  BRG brg_1 (.RS1(RS1), .RS2(RS2), .RD(RD), .MWRITE(MWRITE), .CLK(clk), .DADO(SDADO), .S1(brg_1_s1), .S2(SRS2));
  IMMEXT immext_1 (.E({F7, RS2, RS1, F3, RD}), .TPIMM(TPIMM), .S(SIMM));
  Multiplexer #(.Bits(32)) multiplexer_2 (.sel(IMM), .in_0(SRS2), .in_1(SIMM), .out(multiplexer_2_out));
  // ULA ula_1: pin names not known; wires that end beside it: brg_1_s1, multiplexer_2_out, ULA, SULA, ZERO
  RAMDualPort #(.AddrBits(7), .isProgramMemory("true"), .Bits(32)) MDD (
    .A(SULA[6:0]), .Din(SRS2), .str(STR), .C(clk), .ld(LD), .D(MDD_d));
  Multiplexer #(.Selector_Bits(2), .Bits(32)) multiplexer_3 (
    .sel(DADO), .in_0({32{1'b0}}), .in_1(add_3_s), .in_2(MDD_d), .in_3(SULA), .out(SDADO));
  ADD add_3 (.RS1(32'h4), .RS2(SPC), .S(add_3_s));  // open: Cout

  // Notes on the sheet:
  //   clk: Hz: 20
  //   contents of MI (hex, n*v repeats v):
  //   1400613,0,0,0,100693,0,0,0,100713,0,0,0,d12023,0,0,0,410113,0,0,0
  //   ,e12023,0,0,0,8000ef,7*0,200f93,0,0,0,e13,0,0,0,2cfd063,0,0,0
  //   ,e68e33,0,0,0,410113,0,0,0,1c12023,0,0,0,70693,0,0,0,e0713,0,0,0
  //   ,1f8f93,0,0,0,fe5ff06f,0,0,0,8067
endmodule
