// Digital circuit SLT.dig as structural Verilog
module SLT (
  input  [31:0] RS1,
  input  [31:0] RS2,
  output [31:0] S
);

  wire [30:0] sub_1_s;

  SUB sub_1 (.RS1(RS1), .RS2(RS2), .S({S[31], sub_1_s}));  // open: OF

  assign S[30:0] = {31{S[31]}};
endmodule
