// Digital circuit ULA.dig as structural Verilog
module ULA (
  input  [31:0] RS1,
  input  [31:0] RS2,
  input  [2:0] I,
  output [31:0] S
);

  wire [31:0] add_1_s, and_1_s, or_1_s, or_32_1_s, sll_1_s, slt_1_s, sub_1_s, sub_2_s, xor_1_s;

  SUB sub_1 (.RS1(RS1), .RS2(RS2), .S(sub_1_s));  // open: OF
  ADD add_1 (.RS1(RS1), .RS2(RS2), .S(add_1_s));  // open: Cout
  SUB sub_2 (.RS1(RS1), .RS2(RS2), .S(sub_2_s));  // open: OF
  XOR xor_1 (.RS1(RS1), .RS2(RS2), .S(xor_1_s));
  OR or_1 (.RS1(RS1), .RS2(RS2), .S(or_1_s));
  AND and_1 (.RS1(RS1), .RS2(RS2), .S(and_1_s));
  SLL sll_1 (.RS1(RS1), .RS2(RS2), .S(sll_1_s));
  SLT slt_1 (.RS1(RS1), .RS2(RS2), .S(slt_1_s));
  OR_32 or_32_1 (.E(sub_1_s), .S(or_32_1_s));
  Multiplexer #(.Selector_Bits(3), .Bits(32)) multiplexer_1 (
    .sel(I), .in_0(or_32_1_s), .in_1(add_1_s), .in_2(sub_2_s), .in_3(xor_1_s), .in_4(or_1_s), .in_5(and_1_s),
    .in_6(sll_1_s), .in_7(slt_1_s), .out(S));
endmodule
